// Logisim project alu.circ as structural Verilog: 16 circuits, main circuit main
module main (
  input  [31:0] X,
  input  [31:0] Y,
  input  [3:0] Switch,
  output Signed_Overflow,
  output Equal,
  output [31:0] Result,
  output [31:0] Result_2
);

  wire add_overf, addu_overf, and_overf, divu_overf, mult_overf, nor_overf, or_overf, sll_overf, slt_overf,
       sltu_overf, sra_overf, srl_overf, sub_overf, subu_overf, xor_overf;
  wire [31:0] add_res, add_res2, addu_res, addu_res2, and_res, and_res2, divu_res, divu_res2, mult_res,
       mult_res2, multu_res, multu_res2, nor_res, nor_res2, or_res, or_res2, sll_res, sll_res2, slt_res,
       slt_res2, sltu_res, sltu_res2, sra_res, sra_res2, srl_res, srl_res2, sub_res, sub_res2, subu_res,
       subu_res2, xor_res, xor_res2;

  Comparator #(.width(32)) comparator_1 (.a(X), .b(Y), .eq(Equal));  // open: gt, lt
  sra sra (.X(X), .Y(Y), .overflow(sra_overf), .result(sra_res), .result2(sra_res2));
  srl add (.X(X), .Y(Y), .overflow(add_overf), .result(add_res), .result2(add_res2));
  subu subu (.X(X), .Y(Y), .overflow(subu_overf), .result(subu_res), .result_2(subu_res2));
  \xor  \xor  (.X(X), .Y(Y), .overflow(xor_overf), .result(xor_res), .result_2(xor_res2));
  Multiplexer #(.select(4), .enable("false")) multiplexer_1 (
    .in0(sll_overf), .in1(srl_overf), .in2(sra_overf), .in3(mult_overf), .in4(divu_overf), .in5(add_overf),
    .in6(addu_overf), .in7(sub_overf), .in8(subu_overf), .in9(and_overf), .in10(or_overf), .in11(slt_overf),
    .in12(sltu_overf), .in13(1'b0), .in14(1'b0), .in15(1'b0), .out(Signed_Overflow), .sel(Switch));
  sll sll (.X(X), .Y(Y), .overflow(sll_overf), .result(sll_res), .result2(sll_res2));
  mult mult (.X(X), .Y(Y), .overflow(mult_overf), .result(mult_res), .result_2(mult_res2));
  addu addu (.X(X), .Y(Y), .overflow(addu_overf), .result(addu_res), .result_2(addu_res2));
  \and  \and  (.X(X), .Y(Y), .overflow(and_overf), .result(and_res), .result_2(and_res2));
  \nor  \nor  (.X(X), .Y(Y), .overflow(nor_overf), .result(nor_res), .result_2(nor_res2));
  srl srl (.X(X), .Y(Y), .overflow(srl_overf), .result(srl_res), .result2(srl_res2));
  divu divu (.X(X), .Y(Y), .overflow(divu_overf), .result(divu_res), .result_2(divu_res2));
  sub sub_1 (.X(X), .Y(Y), .overflow(sub_overf), .result(sub_res), .result_2(sub_res2));
  \or  \or  (.X(X), .Y(Y), .overflow(or_overf), .result(or_res), .result_2(or_res2));
  slt slt (.X(X), .Y(Y), .overflow(slt_overf), .result(slt_res), .result_2(slt_res2));
  Multiplexer #(.select(4), .width(32), .enable("false")) multiplexer_2 (
    .in0(sll_res), .in1(srl_res), .in2(sra_res), .in3(multu_res), .in4(divu_res), .in5(add_res),
    .in6(addu_res), .in7(sub_res), .in8(subu_res), .in9(and_res), .in10(or_res), .in11(slt_res),
    .in12(sltu_res), .in13({32{1'b0}}), .in14({32{1'b0}}), .in15({32{1'b0}}), .out(Result), .sel(Switch));
  sltu sltu_1 (.X(X), .Y(Y), .overflow(sltu_overf), .result(sltu_res), .result_2(sltu_res2));
  Multiplexer #(.select(4), .width(32), .enable("false")) multiplexer_3 (
    .in0(sll_res2), .in1(srl_res2), .in2(sra_res2), .in3(multu_res2), .in4(divu_res2), .in5(add_res2),
    .in6(addu_res2), .in7(sub_res2), .in8(subu_res2), .in9(and_res2), .in10(or_res2), .in11(slt_res2),
    .in12(sltu_res2), .in13({32{1'b0}}), .in14({32{1'b0}}), .in15({32{1'b0}}), .out(Result_2), .sel(Switch));

  // Other names for the same wires on the sheet: overflow = Signed_Overflow; S[3:0] = Switch

  // Notes on the sheet:
  //   INPUTS to your circuit
  //   DON'T CHANGE THE LOCATIONS OF THE INPUTS AND OUTPUTS!
  //   OUTPUTS from your circuit
endmodule

module sll (
  input  [31:0] X,
  input  [31:0] Y,
  output overflow,
  output [31:0] result,
  output [31:0] result2
);

  Shifter #(.width(32)) shifter_1 (.in(Y), .\dist (X[4:0]), .out(result));

  assign overflow = 1'b0;
  assign result2 = {32{1'b0}};

  // Other names for the same wires on the sheet: sll_result[31:0] = result; shamt[4:0] = X[4:0];
  //   top_bits[26:0] = X[31:5]
endmodule

module srl (
  input  [31:0] X,
  input  [31:0] Y,
  output overflow,
  output [31:0] result,
  output [31:0] result2
);

  Shifter #(.width(32), .shift("lr")) shifter_1 (.in(Y), .\dist (X[4:0]), .out(result));

  assign overflow = 1'b0;
  assign result2 = {32{1'b0}};

  // Other names for the same wires on the sheet: srl_result[31:0] = result; shamt[4:0] = X[4:0];
  //   top_bits[26:0] = X[31:5]
endmodule

module sra (
  input  [31:0] X,
  input  [31:0] Y,
  output overflow,
  output [31:0] result,
  output [31:0] result2
);

  Shifter #(.width(32), .shift("ar")) shifter_1 (.in(Y), .\dist (X[4:0]), .out(result));

  assign overflow = 1'b0;
  assign result2 = {32{1'b0}};

  // Other names for the same wires on the sheet: sra_result[31:0] = result; shamt[4:0] = X[4:0];
  //   top_bits[26:0] = X[31:5]
endmodule

module mult (
  input  [31:0] X,
  input  [31:0] Y,
  output overflow,
  output [31:0] result,
  output [31:0] result_2
);

  Multiplier #(.width(32)) multiplier_1 (.a(X), .b(Y), .out(result), .cout(result_2));  // open: cin

  assign overflow = 1'b0;

  // Other names for the same wires on the sheet: lower_bits[31:0] = result; upper_bits[31:0] = result_2
endmodule

module divu (
  input  [31:0] X,
  input  [31:0] Y,
  output overflow,
  output [31:0] result,
  output [31:0] result_2
);

  Divider #(.width(32)) divider_1 (.a(X), .b(Y), .out(result), .rem(result_2));  // open: upper

  assign overflow = 1'b0;

  // Other names for the same wires on the sheet: quotient[31:0] = result; remainder[31:0] = result_2
endmodule

module add (
  input  [31:0] X,
  input  [31:0] Y,
  output overflow,
  output [31:0] result,
  output [31:0] result_2
);

  wire check, comparator_2_eq, over;

  Adder #(.width(32)) adder_1 (.a(X), .b(Y), .out(result));  // open: cin, cout
  Multiplexer #(.enable("false")) multiplexer_1 (.in0(1'b0), .in1(over), .out(overflow), .sel(check));
  Comparator #(.width(1), .mode("unsigned")) comparator_1 (.a(X[31]), .b(Y[31]), .eq(check));  // open: gt, lt
  Comparator #(.width(1), .mode("unsigned")) comparator_2 (
    .a(X[31]), .b(result[31]), .eq(comparator_2_eq));  // open: gt, lt
  not not_1 (over, comparator_2_eq);

  assign result_2 = {32{1'b0}};

  // Other names for the same wires on the sheet: overfl = overflow; sum[31:0] = result; significant_sum = result[31];
  //   significantX = X[31]; significantY = Y[31]
endmodule

module addu (
  input  [31:0] X,
  input  [31:0] Y,
  output overflow,
  output [31:0] result,
  output [31:0] result_2
);

  Adder #(.width(32)) adder_1 (.a(X), .b(Y), .out(result));  // open: cin, cout

  assign overflow = 1'b0;
  assign result_2 = {32{1'b0}};

  // Other names for the same wires on the sheet: sum[31:0] = result
endmodule

module sub (
  input  [31:0] X,
  input  [31:0] Y,
  output overflow,
  output [31:0] result,
  output [31:0] result_2
);

  wire [31:0] minus_Y;

  Negator #(.width(32)) negator_1 (.in(Y), .out(minus_Y));
  add add_1 (.X(X), .Y(minus_Y), .overflow(overflow), .result(result), .result_2(result_2));
endmodule

module subu (
  input  [31:0] X,
  input  [31:0] Y,
  output overflow,
  output [31:0] result,
  output [31:0] result_2
);

  Subtractor #(.width(32)) subtractor_1 (.a(X), .b(Y), .out(result));  // open: bin, bout

  assign overflow = 1'b0;
  assign result_2 = {32{1'b0}};

  // Other names for the same wires on the sheet: sum[31:0] = result
endmodule

module \and  (
  input  [31:0] X,
  input  [31:0] Y,
  output overflow,
  output [31:0] result,
  output [31:0] result_2
);

  assign result = X & Y;  // AND_Gate and_1, 32 bits wide

  assign overflow = 1'b0;
  assign result_2 = {32{1'b0}};

  // Other names for the same wires on the sheet: ander[31:0] = result
endmodule

module \or  (
  input  [31:0] X,
  input  [31:0] Y,
  output overflow,
  output [31:0] result,
  output [31:0] result_2
);

  assign result = X | Y;  // OR_Gate or_1, 32 bits wide

  assign overflow = 1'b0;
  assign result_2 = {32{1'b0}};

  // Other names for the same wires on the sheet: result_or[31:0] = result
endmodule

module \xor  (
  input  [31:0] X,
  input  [31:0] Y,
  output overflow,
  output [31:0] result,
  output [31:0] result_2
);

  assign result = X ^ Y;  // XOR_Gate xor_1, 32 bits wide

  assign overflow = 1'b0;
  assign result_2 = {32{1'b0}};

  // Other names for the same wires on the sheet: ander[31:0] = result
endmodule

module \nor  (
  input  [31:0] X,
  input  [31:0] Y,
  output overflow,
  output [31:0] result,
  output [31:0] result_2
);

  assign result = ~(X | Y);  // NOR_Gate nor_1, 32 bits wide

  assign overflow = 1'b0;
  assign result_2 = {32{1'b0}};

  // Other names for the same wires on the sheet: ander[31:0] = result
endmodule

module slt (
  input  [31:0] X,
  input  [31:0] Y,
  output overflow,
  output [31:0] result,
  output [31:0] result_2
);

  wire slt_result;

  Comparator #(.width(32)) comparator_1 (.a(X), .b(Y), .lt(slt_result));  // open: gt, eq
  assign result = {{31{1'b0}}, slt_result};  // Bit_Extender bit_extender_1

  assign overflow = 1'b0;
  assign result_2 = {32{1'b0}};
endmodule

module sltu (
  input  [31:0] X,
  input  [31:0] Y,
  output overflow,
  output [31:0] result,
  output [31:0] result_2
);

  wire slt_result;

  Comparator #(.width(32), .mode("unsigned")) comparator_1 (.a(X), .b(Y), .lt(slt_result));  // open: gt, eq
  assign result = {{31{1'b0}}, slt_result};  // Bit_Extender bit_extender_1

  assign overflow = 1'b0;
  assign result_2 = {32{1'b0}};
endmodule
