// Logisim project cpu.circ as structural Verilog: 2 circuits, main circuit main
module main (
  input  [31:0] INSTRUCTION,
  input  CLOCK,
  output [31:0] FETCH_ADDRESS,
  output [31:0] s0_Value,
  output [31:0] s1_Value,
  output [31:0] s2_Value,
  output [31:0] ra_Value,
  output [31:0] sp_Value,
  output [31:0] HI_Value,
  output [31:0] LO_Value
);

  wire ALU, ALUShift16, ALUSrc, and_1_out, and_6_out, and_7_out, branch, BranchEqs, branchequals,
       BranchNotEqs, comparator_2_eq, ExtOp, Jump, main_2_signed_overflow, MemToReg, MemToRegHiLo, MemWr,
       not_1_out, not_2_out, or_1_out, or_2_out, or_3_out, r_type, ReadFromHi, RegDst, RegDstRa, RegWr,
       shift, write_enable, write_ra, WriteHiLo;
  wire [3:0] ALUCtr;
  wire [4:0] _11_15, _16_20, _21_25, multiplexer_2_out, rt_rd_select, write_reg;
  wire [5:0] _26_31;
  wire [10:0] _0_10;
  wire [27:0] bit_extender_4_out, PC_4;
  wire [31:0] _0_15_SE, bit_extender_1_out, bit_extender_2_out, bit_extender_3_out, branch_addr, jump_addr,
       lui_shift, main_1_read_data_1, main_1_read_data_2, main_2_result, main_2_result_2, MEM_p5,
       multiplexer_1_out, multiplexer_4_out, multiplexer_7_out, multiplexer_8_out, multiplexer_9_out,
       multiplexer_10_out, multiplexer_11_out, multiplexer_12_out, multiplexer_13_out, multiplexer_14_out,
       shifter_2_out;

  Control Control (
    .opcode(_26_31), .funct(_0_10[5:0]), .RegDst(RegDst), .BranchEqs(BranchEqs), .Jump(Jump),
    .BranchNotEqs(BranchNotEqs), .WriteHiLo(WriteHiLo), .ALUShift16(ALUShift16), .MemWr(MemWr),
    .ReadFromHi(ReadFromHi), .MemToReg(MemToReg), .ExtOp(ExtOp), .ALUSrc(ALUSrc),
    .MemToRegHiLo(MemToRegHiLo), .ALUCtr(ALUCtr), .RegWr(RegWr), .RegDstRa(RegDstRa));
  Comparator #(.width(6), .mode("unsigned")) comparator_1 (.a(_26_31), .b({6{1'b0}}), .eq(r_type));  // open: gt, lt
  Register #(.width(32)) register_1 (
    .D(INSTRUCTION), .Q({_26_31, _21_25, _16_20, _11_15, _0_10}), .clk(CLOCK));  // open: en, clr
  Shifter #(.width(32)) shifter_1 (.in(_0_15_SE), .\dist (5'b10000), .out(lui_shift));
  Register #(.width(32)) PC (.D(multiplexer_1_out), .Q(FETCH_ADDRESS), .clk(CLOCK));  // open: en, clr
  Multiplexer #(.width(32)) multiplexer_1 (
    .in0(multiplexer_11_out), .in1(ra_Value), .out(multiplexer_1_out), .en(and_1_out));  // open: sel
  and and_1 (and_1_out, Jump, r_type);
  Multiplexer #(.width(5)) multiplexer_2 (
    .in0(_21_25), .in1(_16_20), .out(multiplexer_2_out), .sel(shift));  // open: en
  Multiplexer #(.width(5)) multiplexer_3 (.in0(_16_20), .in1(_11_15), .out(rt_rd_select), .sel(RegDst));  // open: en
  assign bit_extender_1_out = {{16{1'b0}}, {_11_15, _0_10}};  // Bit_Extender bit_extender_1
  assign bit_extender_2_out = {{16{_11_15[4]}}, {_11_15, _0_10}};  // Bit_Extender bit_extender_2
  not not_1 (not_1_out, comparator_2_eq);
  Comparator #(.width(5), .mode("unsigned")) comparator_2 (
    .a(_0_10[10:6]), .b({5{1'b0}}), .eq(comparator_2_eq));  // open: gt, lt
  or or_1 (or_1_out, write_ra, not_2_out);
  not not_2 (not_2_out, RegDstRa);
  Adder #(.width(32)) adder_1 (.a(32'h4), .b(FETCH_ADDRESS), .out({jump_addr[31:28], PC_4}));  // open: cin, cout
  Multiplexer #(.width(32)) multiplexer_4 (
    .in0(multiplexer_7_out), .in1(FETCH_ADDRESS), .out(multiplexer_4_out), .sel(write_ra));  // open: en
  Multiplexer #(.width(32)) multiplexer_5 (
    .in0(bit_extender_1_out), .in1(bit_extender_2_out), .out(_0_15_SE), .sel(ExtOp));  // open: en
  or or_2 (or_2_out, not_1_out, ALUShift16);
  and and_2 (write_enable, or_1_out, RegWr);
  Multiplexer #(.width(5)) multiplexer_6 (
    .in0(rt_rd_select), .in1({5{1'b1}}), .out(write_reg), .sel(RegDstRa));  // open: en
  regfile_main main_1 (
    .Read_Register_1(multiplexer_2_out), .Read_Register_2(_16_20), .Write_Register(write_reg),
    .Write_Data(multiplexer_4_out), .Write_Enable(write_enable), .Clock(CLOCK),
    .Read_Data_1(main_1_read_data_1), .Read_Data_2(main_1_read_data_2), .s0_Value(s0_Value),
    .s1_Value(s1_Value), .s2_Value(s2_Value), .ra_Value(ra_Value), .sp_Value(sp_Value));
  Multiplexer #(.width(32)) multiplexer_7 (
    .in0(multiplexer_14_out), .in1(lui_shift), .out(multiplexer_7_out), .sel(ALUShift16));  // open: en
  and and_3 (shift, r_type, or_2_out);
  and and_4 (branchequals, ALU, BranchEqs);
  Multiplexer #(.width(32)) multiplexer_8 (
    .in0(main_1_read_data_2), .in1(multiplexer_9_out), .out(multiplexer_8_out), .sel(ALUSrc));  // open: en
  Multiplexer #(.width(32)) multiplexer_9 (
    .in0(_0_15_SE), .in1(bit_extender_3_out), .out(multiplexer_9_out), .en(r_type));  // open: sel
  Multiplexer #(.width(32)) multiplexer_10 (
    .in0({jump_addr[31:28], PC_4}), .in1(branch_addr), .out(multiplexer_10_out), .sel(or_3_out));  // open: en
  or or_3 (or_3_out, branchequals, branch);
  and and_5 (branch, ALU, BranchNotEqs);
  LED led_1 (.in(main_2_signed_overflow));
  alu_main main_2 (
    .Switch(ALUCtr), .X(main_1_read_data_1), .Equal(ALU), .Result(main_2_result),
    .Signed_Overflow(main_2_signed_overflow), .Y(multiplexer_8_out), .Result_2(main_2_result_2));
  assign bit_extender_3_out = {{27{1'b0}}, _0_10[10:6]};  // Bit_Extender bit_extender_3
  Adder #(.width(32)) adder_2 (.a(FETCH_ADDRESS), .b(shifter_2_out), .out(branch_addr));  // open: cin, cout
  Shifter #(.width(32)) shifter_2 (.in(_0_15_SE), .\dist (5'b00010), .out(shifter_2_out));
  and and_6 (and_6_out, branchequals, RegDstRa);
  and and_7 (and_7_out, RegDstRa, BranchEqs);
  or or_4 (write_ra, and_6_out, and_7_out);
  Multiplexer #(.width(32)) multiplexer_11 (
    .in0(multiplexer_10_out), .in1(jump_addr), .out(multiplexer_11_out), .sel(Jump));  // open: en
  Register #(.width(32)) HI (.D(main_2_result_2), .en(WriteHiLo), .Q(HI_Value), .clk(CLOCK));  // open: clr
  Register #(.width(32)) LO (.D(main_2_result), .en(WriteHiLo), .Q(LO_Value), .clk(CLOCK));  // open: clr
  assign bit_extender_4_out = {{2{1'b0}}, {_21_25, _16_20, _11_15, _0_10}};  // Bit_Extender bit_extender_4
  // mem_main MEM: pin names not known; wires that end beside it: main_2_result, main_1_read_data_2, MemWr, CLOCK, MEM_p5
  Shifter #(.width(28)) shifter_3 (.in(bit_extender_4_out), .\dist (5'b00010), .out(jump_addr[27:0]));
  Multiplexer #(.width(32)) multiplexer_12 (
    .in0(main_2_result), .in1(MEM_p5), .out(multiplexer_12_out), .sel(MemToReg));  // open: en
  Multiplexer #(.width(32)) multiplexer_13 (
    .in0(LO_Value), .in1(HI_Value), .out(multiplexer_13_out), .sel(ReadFromHi));  // open: en
  Multiplexer #(.width(32)) multiplexer_14 (
    .in0(multiplexer_12_out), .in1(multiplexer_13_out), .out(multiplexer_14_out), .sel(MemToRegHiLo));  // open: en

  // Other names for the same wires on the sheet: funct[5:0] = _0_10[5:0]; shamt[4:0] = _0_10[10:6]; clk = CLOCK;
  //   fetch_addr[31:0] = FETCH_ADDRESS; PC[31:0] = FETCH_ADDRESS; hi_reg[31:0] = HI_Value;
  //   PC_4[31:28] = jump_addr[31:28]; PC_4_upper[3:0] = jump_addr[31:28]; low_reg[31:0] = LO_Value;
  //   ra[31:0] = ra_Value; s0[31:0] = s0_Value; s1[31:0] = s1_Value; s2[31:0] = s2_Value; sp[31:0] = sp_Value

  // Notes on the sheet:
  //   Output
  //   These are outputs/inputs from run.circ
  //   Inputs
  //   These are DEBUG/TEST outputs from your circuit.
endmodule

module Control (
  input  [5:0] opcode,
  input  [5:0] funct,
  output RegDst,
  output BranchEqs,
  output Jump,
  output BranchNotEqs,
  output WriteHiLo,
  output ALUShift16,
  output MemWr,
  output ReadFromHi,
  output MemToReg,
  output ExtOp,
  output ALUSrc,
  output MemToRegHiLo,
  output [3:0] ALUCtr,
  output RegWr,
  output RegDstRa
);

  wire addi, addiu, andi, j, jr, mflo, not_1_out, not_2_out, not_3_out, not_4_out, not_5_out, not_6_out,
       not_7_out, not_8_out, not_9_out, not_10_out, not_11_out, not_12_out, not_13_out, not_14_out,
       not_15_out, not_16_out, not_17_out, not_18_out, not_19_out, not_20_out, not_21_out, not_22_out,
       not_23_out, not_24_out, not_25_out, not_26_out, not_27_out, not_28_out, not_29_out, not_30_out,
       not_31_out, not_32_out, not_33_out, not_34_out, not_35_out, not_36_out, not_37_out, not_38_out,
       not_39_out, not_40_out, not_41_out, not_42_out, not_43_out, not_44_out, not_45_out, not_46_out,
       not_47_out, not_48_out, not_49_out, not_50_out, not_51_out, not_52_out, not_53_out, not_54_out,
       not_55_out, not_56_out, not_57_out, not_58_out, not_59_out, not_60_out, not_61_out, not_62_out,
       not_63_out, not_64_out, not_65_out, not_66_out, not_67_out, not_68_out, not_69_out, not_70_out,
       not_71_out, not_72_out, not_73_out, not_74_out, not_75_out, not_76_out, not_77_out, not_78_out,
       not_79_out, not_80_out, not_81_out, not_82_out, not_83_out, not_84_out, not_85_out, not_86_out,
       not_87_out, not_88_out, not_89_out, not_90_out, not_91_out, not_92_out, not_93_out, not_94_out,
       not_95_out, not_96_out, not_97_out, not_98_out, not_99_out, not_100_out, not_101_out, not_102_out,
       not_103_out, not_104_out, not_105_out, not_106_out, not_107_out, not_108_out, not_109_out,
       not_110_out, not_111_out, not_112_out, not_113_out, not_114_out, not_115_out, not_116_out,
       not_117_out, not_118_out, not_119_out, not_120_out, not_121_out, not_122_out, not_123_out,
       not_124_out, not_125_out, not_126_out, not_127_out, not_128_out, not_129_out, not_130_out,
       not_131_out, not_132_out, not_133_out, not_134_out, not_135_out, not_136_out, not_137_out,
       not_138_out, not_139_out, not_140_out, not_141_out, not_142_out, not_143_out, not_144_out,
       not_145_out, not_146_out, not_147_out, not_148_out, not_149_out, not_150_out, not_151_out,
       not_152_out, not_153_out, not_154_out, not_155_out, not_156_out, not_157_out, not_158_out,
       not_159_out, not_160_out, not_161_out, not_162_out, not_163_out, not_164_out, not_165_out,
       not_166_out, not_167_out, not_168_out, not_169_out, not_170_out, not_171_out, not_172_out,
       not_173_out, not_174_out, not_175_out, not_176_out, not_177_out, not_178_out, not_179_out,
       not_180_out, not_181_out, not_182_out, not_183_out, not_184_out, not_185_out, not_186_out,
       not_187_out, not_188_out, not_189_out, not_190_out, not_191_out, not_192_out, not_193_out,
       not_194_out, not_195_out, not_196_out, not_197_out, not_198_out, not_199_out, not_200_out,
       not_201_out, not_202_out, not_203_out, not_204_out, not_205_out, not_206_out, not_207_out,
       not_208_out, not_209_out, not_210_out, not_211_out, not_212_out, not_213_out, not_214_out,
       not_215_out, not_216_out, not_217_out, not_218_out, not_219_out, not_220_out, not_221_out,
       not_222_out, not_223_out, not_224_out, not_225_out, not_226_out, not_227_out, ori, rest, slti, sltiu,
       xori;
  wire [3:0] multiplexer_1_out, multiplexer_2_out, multiplexer_3_out;
  wire [4:0] _1stchooser, _2ndchooser, _3rdchooser;

  not not_1 (not_1_out, opcode[0]);
  not not_2 (not_2_out, opcode[1]);
  not not_3 (not_3_out, opcode[2]);
  not not_4 (not_4_out, opcode[3]);
  not not_5 (not_5_out, opcode[4]);
  not not_6 (not_6_out, opcode[5]);
  not not_7 (not_7_out, funct[0]);
  not not_8 (not_8_out, funct[1]);
  not not_9 (not_9_out, funct[2]);
  not not_10 (not_10_out, funct[3]);
  not not_11 (not_11_out, funct[4]);
  not not_12 (not_12_out, funct[5]);
  not not_13 (not_13_out, opcode[0]);
  not not_14 (not_14_out, opcode[1]);
  not not_15 (not_15_out, opcode[2]);
  not not_16 (not_16_out, opcode[3]);
  not not_17 (not_17_out, opcode[4]);
  not not_18 (not_18_out, opcode[5]);
  not not_19 (not_19_out, funct[0]);
  not not_20 (not_20_out, funct[1]);
  not not_21 (not_21_out, funct[2]);
  not not_22 (not_22_out, funct[4]);
  not not_23 (not_23_out, funct[5]);
  not not_24 (not_24_out, opcode[0]);
  not not_25 (not_25_out, opcode[1]);
  not not_26 (not_26_out, opcode[2]);
  not not_27 (not_27_out, opcode[3]);
  not not_28 (not_28_out, opcode[4]);
  not not_29 (not_29_out, opcode[5]);
  not not_30 (not_30_out, funct[0]);
  not not_31 (not_31_out, funct[2]);
  not not_32 (not_32_out, funct[3]);
  not not_33 (not_33_out, funct[5]);
  not not_34 (not_34_out, opcode[0]);
  not not_35 (not_35_out, opcode[1]);
  not not_36 (not_36_out, opcode[2]);
  not not_37 (not_37_out, opcode[3]);
  not not_38 (not_38_out, opcode[4]);
  not not_39 (not_39_out, opcode[5]);
  not not_40 (not_40_out, funct[0]);
  not not_41 (not_41_out, funct[1]);
  not not_42 (not_42_out, funct[2]);
  not not_43 (not_43_out, funct[3]);
  not not_44 (not_44_out, funct[4]);
  not not_45 (not_45_out, opcode[0]);
  not not_46 (not_46_out, opcode[1]);
  not not_47 (not_47_out, opcode[2]);
  not not_48 (not_48_out, opcode[3]);
  not not_49 (not_49_out, opcode[4]);
  not not_50 (not_50_out, opcode[5]);
  not not_51 (not_51_out, funct[2]);
  not not_52 (not_52_out, funct[3]);
  not not_53 (not_53_out, funct[4]);
  not not_54 (not_54_out, opcode[0]);
  not not_55 (not_55_out, opcode[1]);
  not not_56 (not_56_out, opcode[2]);
  not not_57 (not_57_out, opcode[3]);
  not not_58 (not_58_out, opcode[4]);
  not not_59 (not_59_out, opcode[5]);
  not not_60 (not_60_out, funct[0]);
  not not_61 (not_61_out, funct[3]);
  not not_62 (not_62_out, funct[4]);
  not not_63 (not_63_out, opcode[0]);
  not not_64 (not_64_out, opcode[1]);
  not not_65 (not_65_out, opcode[2]);
  not not_66 (not_66_out, opcode[3]);
  not not_67 (not_67_out, opcode[4]);
  not not_68 (not_68_out, opcode[5]);
  not not_69 (not_69_out, funct[2]);
  not not_70 (not_70_out, funct[4]);
  not not_71 (not_71_out, opcode[1]);
  not not_72 (not_72_out, opcode[3]);
  not not_73 (not_73_out, opcode[4]);
  not not_74 (not_74_out, opcode[5]);
  not not_75 (not_75_out, opcode[0]);
  not not_76 (not_76_out, opcode[2]);
  not not_77 (not_77_out, opcode[4]);
  not not_78 (not_78_out, opcode[5]);
  not not_79 (not_79_out, opcode[1]);
  not not_80 (not_80_out, opcode[4]);
  not not_81 (not_81_out, opcode[5]);
  not not_82 (not_82_out, opcode[2]);
  not not_83 (not_83_out, opcode[3]);
  not not_84 (not_84_out, opcode[4]);
  or or_1 (Jump, j, RegDstRa, jr);
  or or_2 (WriteHiLo, _1stchooser[3], _1stchooser[4]);
  and and_1 (_1stchooser[0], not_1_out, not_2_out, not_3_out, not_4_out, not_5_out, not_6_out, not_7_out, not_8_out, not_9_out, not_10_out, not_11_out, not_12_out);
  and and_2 (jr, not_13_out, not_14_out, not_15_out, not_16_out, not_17_out, not_18_out, not_19_out, not_20_out, not_21_out, funct[3], not_22_out, not_23_out);
  and and_3 (mflo, not_24_out, not_25_out, not_26_out, not_27_out, not_28_out, not_29_out, not_30_out, funct[1], not_31_out, not_32_out, funct[4], not_33_out);
  and and_4 (_2ndchooser[0], not_34_out, not_35_out, not_36_out, not_37_out, not_38_out, not_39_out, not_40_out, not_41_out, not_42_out, not_43_out, not_44_out, funct[5]);
  and and_5 (_2ndchooser[3], not_45_out, not_46_out, not_47_out, not_48_out, not_49_out, not_50_out, funct[0], funct[1], not_51_out, not_52_out, not_53_out, funct[5]);
  and and_6 (_3rdchooser[1], not_54_out, not_55_out, not_56_out, not_57_out, not_58_out, not_59_out, not_60_out, funct[1], funct[2], not_61_out, not_62_out, funct[5]);
  and and_7 (_3rdchooser[4], not_63_out, not_64_out, not_65_out, not_66_out, not_67_out, not_68_out, funct[0], funct[1], not_69_out, funct[3], not_70_out, funct[5]);
  and and_8 (BranchNotEqs, opcode[0], not_71_out, opcode[2], not_72_out, not_73_out, not_74_out);
  and and_9 (slti, not_75_out, opcode[1], not_76_out, opcode[3], not_77_out, not_78_out);
  and and_10 (ori, opcode[0], not_79_out, opcode[2], opcode[3], not_80_out, not_81_out);
  and and_11 (MemToReg, opcode[0], opcode[1], not_82_out, not_83_out, not_84_out, opcode[5]);
  or or_3 (ExtOp, BranchEqs, BranchNotEqs, addi, addiu, slti, sltiu, andi, ori, xori, ALUShift16, MemToReg, MemWr);
  or or_4 (RegWr, _1stchooser[0], _1stchooser[1], _1stchooser[2], RegDstRa, ReadFromHi, mflo, _2ndchooser[0], _2ndchooser[1], _2ndchooser[2], _2ndchooser[3], _2ndchooser[4], _3rdchooser[0], _3rdchooser[1], _3rdchooser[2], _3rdchooser[3], _3rdchooser[4], addi, addiu, slti, sltiu, andi, ori, xori, ALUShift16, MemToReg);
  not not_85 (not_85_out, opcode[0]);
  not not_86 (not_86_out, opcode[1]);
  not not_87 (not_87_out, opcode[2]);
  not not_88 (not_88_out, opcode[3]);
  not not_89 (not_89_out, opcode[4]);
  not not_90 (not_90_out, opcode[5]);
  not not_91 (not_91_out, funct[0]);
  not not_92 (not_92_out, funct[2]);
  not not_93 (not_93_out, funct[3]);
  not not_94 (not_94_out, funct[4]);
  not not_95 (not_95_out, funct[5]);
  not not_96 (not_96_out, opcode[2]);
  not not_97 (not_97_out, opcode[3]);
  not not_98 (not_98_out, opcode[4]);
  not not_99 (not_99_out, opcode[5]);
  not not_100 (not_100_out, opcode[0]);
  not not_101 (not_101_out, opcode[1]);
  not not_102 (not_102_out, opcode[2]);
  not not_103 (not_103_out, opcode[3]);
  not not_104 (not_104_out, opcode[4]);
  not not_105 (not_105_out, opcode[5]);
  not not_106 (not_106_out, funct[0]);
  not not_107 (not_107_out, funct[1]);
  not not_108 (not_108_out, funct[2]);
  not not_109 (not_109_out, funct[5]);
  not not_110 (not_110_out, opcode[0]);
  not not_111 (not_111_out, opcode[1]);
  not not_112 (not_112_out, opcode[2]);
  not not_113 (not_113_out, opcode[3]);
  not not_114 (not_114_out, opcode[4]);
  not not_115 (not_115_out, opcode[5]);
  not not_116 (not_116_out, funct[1]);
  not not_117 (not_117_out, funct[2]);
  not not_118 (not_118_out, funct[3]);
  not not_119 (not_119_out, funct[4]);
  not not_120 (not_120_out, opcode[0]);
  not not_121 (not_121_out, opcode[1]);
  not not_122 (not_122_out, opcode[2]);
  not not_123 (not_123_out, opcode[3]);
  not not_124 (not_124_out, opcode[4]);
  not not_125 (not_125_out, opcode[5]);
  not not_126 (not_126_out, funct[0]);
  not not_127 (not_127_out, funct[1]);
  not not_128 (not_128_out, funct[3]);
  not not_129 (not_129_out, funct[4]);
  not not_130 (not_130_out, opcode[0]);
  not not_131 (not_131_out, opcode[1]);
  not not_132 (not_132_out, opcode[2]);
  not not_133 (not_133_out, opcode[3]);
  not not_134 (not_134_out, opcode[4]);
  not not_135 (not_135_out, opcode[5]);
  not not_136 (not_136_out, funct[3]);
  not not_137 (not_137_out, funct[4]);
  not not_138 (not_138_out, opcode[0]);
  not not_139 (not_139_out, opcode[2]);
  not not_140 (not_140_out, opcode[3]);
  not not_141 (not_141_out, opcode[4]);
  not not_142 (not_142_out, opcode[5]);
  not not_143 (not_143_out, opcode[0]);
  not not_144 (not_144_out, opcode[1]);
  not not_145 (not_145_out, opcode[2]);
  not not_146 (not_146_out, opcode[4]);
  not not_147 (not_147_out, opcode[5]);
  not not_148 (not_148_out, opcode[2]);
  not not_149 (not_149_out, opcode[4]);
  not not_150 (not_150_out, opcode[5]);
  not not_151 (not_151_out, opcode[0]);
  not not_152 (not_152_out, opcode[4]);
  not not_153 (not_153_out, opcode[5]);
  not not_154 (not_154_out, opcode[2]);
  not not_155 (not_155_out, opcode[4]);
  and and_12 (_1stchooser[1], not_85_out, not_86_out, not_87_out, not_88_out, not_89_out, not_90_out, not_91_out, funct[1], not_92_out, not_93_out, not_94_out, not_95_out);
  and and_13 (RegDstRa, opcode[0], opcode[1], not_96_out, not_97_out, not_98_out, not_99_out);
  and and_14 (_1stchooser[3], not_100_out, not_101_out, not_102_out, not_103_out, not_104_out, not_105_out, not_106_out, not_107_out, not_108_out, funct[3], funct[4], not_109_out);
  and and_15 (_2ndchooser[1], not_110_out, not_111_out, not_112_out, not_113_out, not_114_out, not_115_out, funct[0], not_116_out, not_117_out, not_118_out, not_119_out, funct[5]);
  and and_16 (_2ndchooser[4], not_120_out, not_121_out, not_122_out, not_123_out, not_124_out, not_125_out, not_126_out, not_127_out, funct[2], not_128_out, not_129_out, funct[5]);
  and and_17 (_3rdchooser[2], not_130_out, not_131_out, not_132_out, not_133_out, not_134_out, not_135_out, funct[0], funct[1], funct[2], not_136_out, not_137_out, funct[5]);
  and and_18 (j, not_138_out, opcode[1], not_139_out, not_140_out, not_141_out, not_142_out);
  and and_19 (addi, not_143_out, not_144_out, not_145_out, opcode[3], not_146_out, not_147_out);
  and and_20 (sltiu, opcode[0], opcode[1], not_148_out, opcode[3], not_149_out, not_150_out);
  and and_21 (xori, not_151_out, opcode[1], opcode[2], opcode[3], not_152_out, not_153_out);
  and and_22 (MemWr, opcode[0], opcode[1], not_154_out, opcode[3], not_155_out, opcode[5]);
  or or_5 (ALUSrc, addi, addiu, slti, sltiu, andi, ori, xori, ALUShift16, MemToReg, MemWr);
  Multiplexer #(.select(5), .width(4)) multiplexer_1 (
    .in0(4'b0000), .in1(4'b0000), .in2(4'b0001), .in3(4'b0000), .in4(4'b0010), .in5(4'b0000), .in6(4'b0000),
    .in7(4'b0000), .in8(4'b0011), .in9(4'b0000), .in10(4'b0000), .in11(4'b0000), .in12(4'b0000),
    .in13(4'b0000), .in14(4'b0000), .in15(4'b0000), .in16(4'b0100), .in17(4'b0000), .in18(4'b0000),
    .in19(4'b0000), .in20(4'b0000), .in21(4'b0000), .in22(4'b0000), .in23(4'b0000), .in24(4'b0000),
    .in25(4'b0000), .in26(4'b0000), .in27(4'b0000), .in28(4'b0000), .in29(4'b0000), .in30(4'b0000),
    .in31(4'b0000), .out(multiplexer_1_out), .sel(_1stchooser));  // open: en
  not not_156 (not_156_out, opcode[0]);
  not not_157 (not_157_out, opcode[1]);
  not not_158 (not_158_out, opcode[2]);
  not not_159 (not_159_out, opcode[3]);
  not not_160 (not_160_out, opcode[4]);
  not not_161 (not_161_out, opcode[5]);
  not not_162 (not_162_out, funct[2]);
  not not_163 (not_163_out, funct[3]);
  not not_164 (not_164_out, funct[4]);
  not not_165 (not_165_out, funct[5]);
  not not_166 (not_166_out, opcode[0]);
  not not_167 (not_167_out, opcode[1]);
  not not_168 (not_168_out, opcode[2]);
  not not_169 (not_169_out, opcode[3]);
  not not_170 (not_170_out, opcode[4]);
  not not_171 (not_171_out, opcode[5]);
  not not_172 (not_172_out, funct[0]);
  not not_173 (not_173_out, funct[1]);
  not not_174 (not_174_out, funct[2]);
  not not_175 (not_175_out, funct[3]);
  not not_176 (not_176_out, funct[5]);
  not not_177 (not_177_out, opcode[0]);
  not not_178 (not_178_out, opcode[1]);
  not not_179 (not_179_out, opcode[2]);
  not not_180 (not_180_out, opcode[3]);
  not not_181 (not_181_out, opcode[4]);
  not not_182 (not_182_out, opcode[5]);
  not not_183 (not_183_out, funct[2]);
  not not_184 (not_184_out, funct[5]);
  not not_185 (not_185_out, opcode[0]);
  not not_186 (not_186_out, opcode[1]);
  not not_187 (not_187_out, opcode[2]);
  not not_188 (not_188_out, opcode[3]);
  not not_189 (not_189_out, opcode[4]);
  not not_190 (not_190_out, opcode[5]);
  not not_191 (not_191_out, funct[0]);
  not not_192 (not_192_out, funct[2]);
  not not_193 (not_193_out, funct[3]);
  not not_194 (not_194_out, funct[4]);
  not not_195 (not_195_out, opcode[0]);
  not not_196 (not_196_out, opcode[1]);
  not not_197 (not_197_out, opcode[2]);
  not not_198 (not_198_out, opcode[3]);
  not not_199 (not_199_out, opcode[4]);
  not not_200 (not_200_out, opcode[5]);
  not not_201 (not_201_out, funct[1]);
  not not_202 (not_202_out, funct[3]);
  not not_203 (not_203_out, funct[4]);
  not not_204 (not_204_out, opcode[0]);
  not not_205 (not_205_out, opcode[1]);
  not not_206 (not_206_out, opcode[2]);
  not not_207 (not_207_out, opcode[3]);
  not not_208 (not_208_out, opcode[4]);
  not not_209 (not_209_out, opcode[5]);
  not not_210 (not_210_out, funct[0]);
  not not_211 (not_211_out, funct[2]);
  not not_212 (not_212_out, funct[4]);
  not not_213 (not_213_out, opcode[0]);
  not not_214 (not_214_out, opcode[1]);
  not not_215 (not_215_out, opcode[3]);
  not not_216 (not_216_out, opcode[4]);
  not not_217 (not_217_out, opcode[5]);
  not not_218 (not_218_out, opcode[1]);
  not not_219 (not_219_out, opcode[2]);
  not not_220 (not_220_out, opcode[4]);
  not not_221 (not_221_out, opcode[5]);
  not not_222 (not_222_out, opcode[0]);
  not not_223 (not_223_out, opcode[1]);
  not not_224 (not_224_out, opcode[4]);
  not not_225 (not_225_out, opcode[5]);
  not not_226 (not_226_out, opcode[4]);
  not not_227 (not_227_out, opcode[5]);
  or or_6 (MemToRegHiLo, ReadFromHi, mflo);
  and and_23 (_1stchooser[2], not_156_out, not_157_out, not_158_out, not_159_out, not_160_out, not_161_out, funct[0], funct[1], not_162_out, not_163_out, not_164_out, not_165_out);
  and and_24 (ReadFromHi, not_166_out, not_167_out, not_168_out, not_169_out, not_170_out, not_171_out, not_172_out, not_173_out, not_174_out, not_175_out, funct[4], not_176_out);
  and and_25 (_1stchooser[4], not_177_out, not_178_out, not_179_out, not_180_out, not_181_out, not_182_out, funct[0], funct[1], not_183_out, funct[3], funct[4], not_184_out);
  and and_26 (_2ndchooser[2], not_185_out, not_186_out, not_187_out, not_188_out, not_189_out, not_190_out, not_191_out, funct[1], not_192_out, not_193_out, not_194_out, funct[5]);
  and and_27 (_3rdchooser[0], not_195_out, not_196_out, not_197_out, not_198_out, not_199_out, not_200_out, funct[0], not_201_out, funct[2], not_202_out, not_203_out, funct[5]);
  and and_28 (_3rdchooser[3], not_204_out, not_205_out, not_206_out, not_207_out, not_208_out, not_209_out, not_210_out, funct[1], not_211_out, funct[3], not_212_out, funct[5]);
  and and_29 (BranchEqs, not_213_out, not_214_out, opcode[2], not_215_out, not_216_out, not_217_out);
  and and_30 (addiu, opcode[0], not_218_out, not_219_out, opcode[3], not_220_out, not_221_out);
  and and_31 (andi, not_222_out, not_223_out, opcode[2], opcode[3], not_224_out, not_225_out);
  and and_32 (ALUShift16, opcode[0], opcode[1], opcode[2], opcode[3], not_226_out, not_227_out);
  Multiplexer #(.select(5), .width(4)) multiplexer_2 (
    .in0(multiplexer_1_out), .in1(4'b0101), .in2(4'b0110), .in3(4'b0000), .in4(4'b0111), .in5(4'b0000),
    .in6(4'b0000), .in7(4'b0000), .in8(4'b1000), .in9(4'b0000), .in10(4'b0000), .in11(4'b0000),
    .in12(4'b0000), .in13(4'b0000), .in14(4'b0000), .in15(4'b0000), .in16(4'b1001), .in17(4'b0000),
    .in18(4'b0000), .in19(4'b0000), .in20(4'b0000), .in21(4'b0000), .in22(4'b0000), .in23(4'b0000),
    .in24(4'b0000), .in25(4'b0000), .in26(4'b0000), .in27(4'b0000), .in28(4'b0000), .in29(4'b0000),
    .in30(4'b0000), .in31(4'b0000), .out(multiplexer_2_out), .sel(_2ndchooser));  // open: en
  or or_7 (RegDst, _1stchooser[0], _1stchooser[1], _1stchooser[2], ReadFromHi, mflo, _2ndchooser[0], _2ndchooser[1], _2ndchooser[2], _2ndchooser[3], _2ndchooser[4], _3rdchooser[0], _3rdchooser[1], _3rdchooser[2], _3rdchooser[3], _3rdchooser[4]);
  Multiplexer #(.select(5), .width(4)) multiplexer_3 (
    .in0(multiplexer_2_out), .in1(4'b1010), .in2(4'b1011), .in3(4'b0000), .in4(4'b1100), .in5(4'b0000),
    .in6(4'b0000), .in7(4'b0000), .in8(4'b1101), .in9(4'b0000), .in10(4'b0000), .in11(4'b0000),
    .in12(4'b0000), .in13(4'b0000), .in14(4'b0000), .in15(4'b0000), .in16(4'b1110), .in17(4'b0000),
    .in18(4'b0000), .in19(4'b0000), .in20(4'b0000), .in21(4'b0000), .in22(4'b0000), .in23(4'b0000),
    .in24(4'b0000), .in25(4'b0000), .in26(4'b0000), .in27(4'b0000), .in28(4'b0000), .in29(4'b0000),
    .in30(4'b0000), .in31(4'b0000), .out(multiplexer_3_out), .sel(_3rdchooser));  // open: en
  Multiplexer #(.width(4)) multiplexer_4 (
    .in0(multiplexer_3_out), .in1(4'b1111), .out(ALUCtr), .sel(rest));  // open: en
  or or_8 (rest, jr, RegDstRa, ReadFromHi, mflo, j, BranchEqs, BranchNotEqs, addi, addiu, slti, sltiu, andi, ori, xori, ALUShift16, MemToReg, MemWr);

  // Other names for the same wires on the sheet: sll = _1stchooser[0]; srl = _1stchooser[1]; sra = _1stchooser[2];
  //   mult = _1stchooser[3]; divu = _1stchooser[4]; add = _2ndchooser[0]; addu = _2ndchooser[1]; sub = _2ndchooser[2];
  //   subu = _2ndchooser[3]; and = _2ndchooser[4]; or = _3rdchooser[0]; xor = _3rdchooser[1]; nor = _3rdchooser[2];
  //   slt = _3rdchooser[3]; sltu = _3rdchooser[4]; beq = BranchEqs; bne = BranchNotEqs; func0 = funct[0];
  //   func1 = funct[1]; func2 = funct[2]; func3 = funct[3]; func4 = funct[4]; func5 = funct[5]; jal = RegDstRa;
  //   lui = ALUShift16; lw = MemToReg; mfhi = ReadFromHi; op0 = opcode[0]; op1 = opcode[1]; op2 = opcode[2];
  //   op3 = opcode[3]; op4 = opcode[4]; op5 = opcode[5]; sw = MemWr
endmodule
